# Fritzing sketch dht11Shield (saved by Fritzing 0.9.3b)

parts:
  WeMos_D1_Mini_Protoboard_Shield1 = WeMos D1 Mini Protoboard Shield
  DHT1 = DHT11 Humitidy and Temperature Sensor

nets:
  3V3: WeMos_D1_Mini_Protoboard_Shield1.3V3, WeMos_D1_Mini_Protoboard_Shield1.X3-Y10, DHT1.VDD
  N1: WeMos_D1_Mini_Protoboard_Shield1.D3, WeMos_D1_Mini_Protoboard_Shield1.X5-Y10, DHT1.NULL
  N2: WeMos_D1_Mini_Protoboard_Shield1.G, WeMos_D1_Mini_Protoboard_Shield1.X6-Y10, DHT1.GND
  N3: WeMos_D1_Mini_Protoboard_Shield1.X4-Y10, DHT1.DATA

custom parts:
  DHT11 Humitidy and Temperature Sensor: DHT11 Humidity and Temperature Sensor
